# Fritzing sketch gas alarm (saved by Fritzing 0.9.3b)
breadboards: 1

parts:
  Part1 = Arduino Uno (Rev3)
  o1 = Module display OLED I2C 128x64 SSD1306 [package=THT]
  Keypad4x1 = Keypad Membran 4x4
  M1 = sim800L v2 evb
  Part2 = MQ-9 breakout
  SP1 = SPEAKER [package=pcb_mount_speaker]

nets:
  N1: Part1.A0, Part2.VCC
  N2: Part1.A4/SDA, o1.SDA
  N3: Part1.A5/SCL, o1.SCL
  N4: Part1.D8, Keypad4x1.Pin2
  N5: Part1.D9_PWM, Keypad4x1.Pin1
  N6: Part1.D10_PWM/SS, SP1.-
  N7: Part1.D11_PWM/MOSI, Part2.DO
  N8: Part1.D12/MISO, M1.pin_4
  N9: Part1.D13/SCK, M1.pin_3
  N10: Part1.D2, Keypad4x1.Pin8
  N11: Part1.D3_PWM, Keypad4x1.Pin7
  N12: Part1.D4, Keypad4x1.Pin6
  N13: Part1.D5_PWM, Keypad4x1.Pin5
  N14: Part1.D6_PWM, Keypad4x1.Pin4
  N15: Part1.D7, Keypad4x1.Pin3
  GND: o1.GND, M1.pin_2, M1.pin_6, Part2.GND, SP1.+
  N16: o1.VCC, M1.pin_7

custom parts:
  Module display OLED I2C 128x64 SSD1306: Ecran OLED I2C SSD163 de 128x64 avec connexion I2C
  Keypad Membran 4x4: Membrane Keypad 4x4 Matrix
  sim800L v2 evb: sim800L v2 evb GSM module.
  MQ-9 breakout: SKU: 101284
